# Fritzing sketch Pacer (saved by Fritzing 0.8.7b)
breadboards: 1

parts:
  Raspberry_Pi_1 = Raspberry Pi 3 [part_number=RPI-3-V1.2]
  M1 = fc-51 [package=THT]
  M2 = fc-51 [package=THT]
  Part2 = PWM Shield
  J1 = Basic Servo
  M3 = DC Motor [part_number=ESC]
  Part3 = FTDI Basic Programmer

nets:
  N1: Raspberry_Pi_1.3v3, M1.pin3, M2.pin3
  N2: Raspberry_Pi_1.GPIO2, Part2.GSCLK
  N3: Raspberry_Pi_1.GPIO3, Part2.SCLK
  GND: Raspberry_Pi_1.GND, M1.pin2, M2.pin2, Part2.GND, J1.gnd, M3.pin_2, Part3.GND
  N4: Raspberry_Pi_1.GIPO23, M2.pin1
  N5: Raspberry_Pi_1.GIPO18, M1.pin1
  N6: Raspberry_Pi_1.GIPO15, Part3.DTR
  N7: Raspberry_Pi_1.GIPO14, Part3.RXI
  VCC: Raspberry_Pi_1.5V, Part2.VCC, J1.vcc, M3.pin_1
  N8: Part2.OUT0, J1.pulse

notes:
  SDA
  SLK
  Serial Cable to PC
  ESC >>> Titan 12T Motor
  Steering Servo
  IR Sensors
